# Fritzing sketch wiring (saved by Fritzing 0.9.4)

parts:
  A1 = Waveshare rp2040-zero tht [package=THT]
  U1 = WS2812 RGB LED strip
  Mod1 = flyskyr6b

nets:
  VCC: A1.Pin_1, U1.VCC, Mod1.VCC
  GND: A1.Pin_2, U1.GND, Mod1.connector14, Mod1.GND
  N1: A1.Pin_4, Mod1.CH1
  N2: A1.Pin_5, Mod1.CH2
  N3: A1.Pin_6, U1.DIN

custom parts:
  Waveshare rp2040-zero tht: .RP2040-Zero, A Low-Cost, High-Performance Pico-Like MCU Board Based On Raspberry Pi Microcontroller RP2040. This varant is THT without the extra connections.
  WS2812 RGB LED strip: WS2812 strip
  flyskyr6b: flysky r6b 6ch rc receiver module. Pcb view is 3*7 header pins, 3 female headers will let the board plug in to the receiver, or connect via wires as you choose.
